# Fritzing sketch snort (saved by Fritzing 0.8.3b)
breadboards: 1

parts:
  Raspberry_Pi_rev1 = Raspberry Pi rev1
  ON/OFF = Waterproof Pushbutton (red)
  R1 = Resistor [tolerance=±5% resistance=330 package=THT]
  R2 = Resistor [tolerance=±5% resistance=10k package=THT]
  R3 = Resistor [tolerance=±5% resistance=10k package=THT]
  MOTION_SENSOR = PIR sensor
  R4 = Resistor [tolerance=±5% resistance=10k package=THT]

nets:
  N1: Raspberry_Pi_rev1.3V3, ON/OFF.no_name_yet#1
  5V: Raspberry_Pi_rev1.5V, MOTION_SENSOR.VDD
  GND: Raspberry_Pi_rev1.GND, ON/OFF.no_name_yet#5, MOTION_SENSOR.GND
  N2: Raspberry_Pi_rev1.GPIO_23, R1.Pin_1
  N3: Raspberry_Pi_rev1.GPIO_21, R2.Pin_1
  N4: Raspberry_Pi_rev1.GPIO22, R3.Pin_1
  N5: Raspberry_Pi_rev1.GPIO_25, R4.Pin_1
  N6: ON/OFF.no_name_yet#2, R3.Pin_0
  N7: ON/OFF.no_name_yet#3, R2.Pin_0
  N8: ON/OFF.no_name_yet#4, R1.Pin_0
  N9: MOTION_SENSOR.SIG, R4.Pin_0

custom parts:
  Waterproof Pushbutton (red): Waterproof Illuminated Pushbutton (red)
